// Digital circuit circuito_exp2_ativ2.dig as structural Verilog
module circuito_exp2_ativ2 (
  input  ZERA,
  input  CARREGA,
  input  CONTA,
  input  CLOCK,
  input  [3:0] DADO,
  input  Zera_2,
  input  Carrega_2,
  input  Conta_2,
  input  [3:0] Dado_2,
  output [3:0] CONTAGEM,
  output FIM,
  output MENOR,
  output MAIOR,
  output IGUAL,
  output [3:0] Contagem_2
);

  wire Clock_out, not_1_out, not_2_out, u_circuito_exp2_ativ2_fim, u_circuito_exp2_ativ2_igual,
       u_circuito_exp2_ativ2_maior, u_circuito_exp2_ativ2_menor;

  not not_1 (not_1_out, ZERA);
  not not_2 (not_2_out, CARREGA);
  Button u_Clock (.out(Clock_out));
  circuito_exp2_ativ2 #(.applicationType("IVERILOG")) u_circuito_exp2_ativ2 (
    .clock(Clock_out), .zera(Zera_2), .carrega(Carrega_2), .conta(Conta_2), .chaves(Dado_2),
    .menor(u_circuito_exp2_ativ2_menor), .maior(u_circuito_exp2_ativ2_maior),
    .igual(u_circuito_exp2_ativ2_igual), .fim(u_circuito_exp2_ativ2_fim), .db_contagem(Contagem_2));
  contador_163 #(.applicationType("IVERILOG")) u_contador_163 (
    .clock(CLOCK), .clr(not_1_out), .ld(not_2_out), .ent(CONTA), .enp(1'b1), .D(DADO), .Q(CONTAGEM), .rco(FIM));
  LED u_Menor (.in(u_circuito_exp2_ativ2_menor));
  LED u_Maior (.in(u_circuito_exp2_ativ2_maior));
  LED u_Igual (.in(u_circuito_exp2_ativ2_igual));
  LED u_Fim (.in(u_circuito_exp2_ativ2_fim));
  comparador_85 #(.applicationType("IVERILOG")) u_comparador_85 (
    .A(CONTAGEM), .B(DADO), .ALBi(1'b0), .AGBi(1'b0), .AEBi(1'b1), .ALBo(MENOR), .AGBo(MAIOR), .AEBo(IGUAL));
endmodule

/* Code of circuito_exp2_ativ2:
/*
 * ------------------------------------------------------------------
 *  Arquivo   : circuito_exp2_ativ2-PARCIAL.v
 *  Projeto   : Experiencia 2 - Um Fluxo de Dados Simples
 * ------------------------------------------------------------------
 *  Descricao : Circuito PARCIAL do fluxo de dados da Atividade 2
 * 
 *     1) COMPLETAR DESCRICAO
 * 
 * ------------------------------------------------------------------
 *  Revisoes  :
 *      Data        Versao  Autor             Descricao
 *      11/01/2024  1.0     Edson Midorikawa  versao inicial
 * ------------------------------------------------------------------
 * /

module circuito_exp2_ativ2 (clock, zera, carrega, conta, chaves, 
                            menor, maior, igual, fim, db_contagem);
    input        clock;
    input        zera;
    input        carrega;
    input        conta;
    input  [3:0] chaves;
    output       menor;
    output       maior;
    output       igual;
    output       fim;
    output [3:0] db_contagem;

    wire   [3:0] s_contagem;  // sinal interno para interligacao dos componentes

    // contador_163
    contador_163 contador (
      .clock( clock ),
      .clr  ( ~zera ),
      .ld   ( ~carrega ),
      .ent  ( 1'b1 ),
      .enp  ( conta ),
      .D    ( chaves ),
      .Q    ( s_contagem ),
      .rco  ( fim )
    );

    // comparador_85
    comparador_85 comparador (
      .A   ( s_contagem ),
      .B   ( chaves ),
      .ALBi( 1'b0 ),
      .AGBi( 1'b0 ),
      .AEBi( 1'b1 ),
      .ALBo( menor ),
      .AGBo( maior ),
      .AEBo( igual )
    );

    // saida de depuracao
    assign db_contagem = s_contagem;

 endmodule
//------------------------------------------------------------------
// Arquivo   : contador_163.v
/* -----------------------------------------------------------------
 *  Arquivo   : comparador_85.v
 *  Projeto   : Experiencia 2 - Um Fluxo de Dados Simples
 * -----------------------------------------------------------------
 * Descricao : comparador de magnitude de 4 bits 
 *             similar ao CI 7485
 *             baseado em descricao comportamental disponivel em	
 * https://web.eecs.umich.edu/~jhayes/iscas.restore/74L85b.v
 * -----------------------------------------------------------------
 * Revisoes  :
 *     Data        Versao  Autor             Descricao
 *     21/12/2023  1.0     Edson Midorikawa  criacao
 * -----------------------------------------------------------------
 * /

module comparador_85 (ALBi, AGBi, AEBi, A, B, ALBo, AGBo, AEBo);

    input[3:0] A, B;
    input      ALBi, AGBi, AEBi;
    output     ALBo, AGBo, AEBo;
    wire[4:0]  CSL, CSG;

    assign CSL  = ~A + B + ALBi;
    assign ALBo = ~CSL[4];
    assign CSG  = A + ~B + AGBi;
    assign AGBo = ~CSG[4];
    assign AEBo = ((A == B) && AEBi);

endmodule /* comparador_85 * /
// Projeto   : Experiencia 2 - Um Fluxo de Dados Simples
//------------------------------------------------------------------
// Descricao : Contador binario de 4 bits, modulo 16
//             similar ao componente 74163
//
// baseado no componente Vrcntr4u.v do livro Digital Design Principles 
// and Practices, Fifth Edition, by John F. Wakerly              
//------------------------------------------------------------------
// Revisoes  :
//     Data        Versao  Autor             Descricao
//     14/12/2023  1.0     Edson Midorikawa  versao inicial
//------------------------------------------------------------------
//
module contador_163 ( clock, clr, ld, ent, enp, D, Q, rco );
    input clock, clr, ld, ent, enp;
    input [3:0] D;
    output reg [3:0] Q;
    output reg rco;

    always @ (posedge clock)
        if (~clr)               Q <= 4'd0;
        else if (~ld)           Q <= D;
        else if (ent && enp)    Q <= Q + 1'b1;
        else                    Q <= Q;
 
    always @ (Q or ent)
        if (ent && (Q == 4'd15))   rco = 1;
        else                       rco = 0;
endmodule
*/

/* Code of contador_163:
//------------------------------------------------------------------
// Arquivo   : contador_163.v
// Projeto   : Experiencia 2 - Um Fluxo de Dados Simples
//------------------------------------------------------------------
// Descricao : Contador binario de 4 bits, modulo 16
//             similar ao componente 74163
//
// baseado no componente Vrcntr4u.v do livro Digital Design Principles 
// and Practices, Fifth Edition, by John F. Wakerly              
//------------------------------------------------------------------
// Revisoes  :
//     Data        Versao  Autor             Descricao
//     14/12/2023  1.0     Edson Midorikawa  versao inicial
//------------------------------------------------------------------
//
module contador_163 ( clock, clr, ld, ent, enp, D, Q, rco );
    input clock, clr, ld, ent, enp;
    input [3:0] D;
    output reg [3:0] Q;
    output reg rco;

    always @ (posedge clock)
        if (~clr)               Q <= 4'd0;
        else if (~ld)           Q <= D;
        else if (ent && enp)    Q <= Q + 1'b1;
        else                    Q <= Q;
 
    always @ (Q or ent)
        if (ent && (Q == 4'd15))   rco = 1;
        else                       rco = 0;
endmodule
*/

/* Code of comparador_85:
/* -----------------------------------------------------------------
 *  Arquivo   : comparador_85.v
 *  Projeto   : Experiencia 2 - Um Fluxo de Dados Simples
 * -----------------------------------------------------------------
 * Descricao : comparador de magnitude de 4 bits 
 *             similar ao CI 7485
 *             baseado em descricao comportamental disponivel em	
 * https://web.eecs.umich.edu/~jhayes/iscas.restore/74L85b.v
 * -----------------------------------------------------------------
 * Revisoes  :
 *     Data        Versao  Autor             Descricao
 *     21/12/2023  1.0     Edson Midorikawa  criacao
 * -----------------------------------------------------------------
 * /

module comparador_85 (ALBi, AGBi, AEBi, A, B, ALBo, AGBo, AEBo);

    input[3:0] A, B;
    input      ALBi, AGBi, AEBi;
    output     ALBo, AGBo, AEBo;
    wire[4:0]  CSL, CSG;

    assign CSL  = ~A + B + ALBi;
    assign ALBo = ~CSL[4];
    assign CSG  = A + ~B + AGBi;
    assign AGBo = ~CSG[4];
    assign AEBo = ((A == B) && AEBi);

endmodule /* comparador_85 * /
*/
