// Digital circuit circuito_exp2_desafio.dig as structural Verilog
module circuito_exp2_desafio (
  input  ZERA,
  input  CARREGA,
  input  CONTA,
  input  CLOCK,
  input  [3:0] DADO,
  output FIM,
  output MENOR,
  output MAIOR,
  output IGUAL
);

  wire not_1_out, not_2_out;
  wire [3:0] u_contador_163_q;

  not not_1 (not_1_out, ZERA);
  not not_2 (not_2_out, CARREGA);
  contador_163 #(.applicationType("IVERILOG")) u_contador_163 (
    .clock(CLOCK), .clr(not_1_out), .ld(not_2_out), .ent(CONTA), .enp(1'b1), .D(DADO), .Q(u_contador_163_q),
    .rco(FIM));
  Seven_Seg_Hex seven_seg_hex_1 (.d(u_contador_163_q), .dp(1'b1));
  comparador_85 #(.applicationType("IVERILOG")) u_comparador_85 (
    .A(u_contador_163_q), .B(DADO), .ALBi(1'b0), .AGBi(1'b0), .AEBi(1'b1), .ALBo(MENOR), .AGBo(MAIOR),
    .AEBo(IGUAL));
endmodule

/* Code of contador_163:
//------------------------------------------------------------------
// Arquivo   : contador_163.v
// Projeto   : Experiencia 2 - Um Fluxo de Dados Simples
//------------------------------------------------------------------
// Descricao : Contador binario de 4 bits, modulo 16
//             similar ao componente 74163
//
// baseado no componente Vrcntr4u.v do livro Digital Design Principles 
// and Practices, Fifth Edition, by John F. Wakerly              
//------------------------------------------------------------------
// Revisoes  :
//     Data        Versao  Autor             Descricao
//     14/12/2023  1.0     Edson Midorikawa  versao inicial
//------------------------------------------------------------------
//
module contador_163 ( clock, clr, ld, ent, enp, D, Q, rco );
    input clock, clr, ld, ent, enp;
    input [3:0] D;
    output reg [3:0] Q;
    output reg rco;

    always @ (posedge clock)
        if (~clr)               Q <= 4'd0;
        else if (~ld)           Q <= D;
        else if (ent && enp)    Q <= Q + 1'b1;
        else                    Q <= Q;
 
    always @ (Q or ent)
        if (ent && (Q == 4'd15))   rco = 1;
        else                       rco = 0;
endmodule
*/

/* Code of comparador_85:
/* -----------------------------------------------------------------
 *  Arquivo   : comparador_85.v
 *  Projeto   : Experiencia 2 - Um Fluxo de Dados Simples
 * -----------------------------------------------------------------
 * Descricao : comparador de magnitude de 4 bits 
 *             similar ao CI 7485
 *             baseado em descricao comportamental disponivel em	
 * https://web.eecs.umich.edu/~jhayes/iscas.restore/74L85b.v
 * -----------------------------------------------------------------
 * Revisoes  :
 *     Data        Versao  Autor             Descricao
 *     21/12/2023  1.0     Edson Midorikawa  criacao
 * -----------------------------------------------------------------
 * /

module comparador_85 (ALBi, AGBi, AEBi, A, B, ALBo, AGBo, AEBo);

    input[3:0] A, B;
    input      ALBi, AGBi, AEBi;
    output     ALBo, AGBo, AEBo;
    wire[4:0]  CSL, CSG;

    assign CSL  = ~A + B + ALBi;
    assign ALBo = ~CSL[4];
    assign CSG  = A + ~B + AGBi;
    assign AGBo = ~CSG[4];
    assign AEBo = ((A == B) && AEBi);

endmodule /* comparador_85 * /
*/
