// Digital circuit comparador_85_testado.dig as structural Verilog
module comparador_85_testado (
  input  in_1,
  input  in_2,
  input  in_3,
  input  [3:0] in_4,
  input  [3:0] in_5
);

  wire u_comparador_85_aebo, u_comparador_85_agbo, u_comparador_85_albo;

  comparador_85 #(.applicationType("IVERILOG"), .CodeFile("C:\\Users\\gabri\\CODE\\VERILOG\\QUARTUS\\LAB02\\comparador_85.v")) u_comparador_85 (
    .A(in_5), .B(in_4), .ALBi(in_1), .AGBi(in_2), .AEBi(in_3), .ALBo(u_comparador_85_albo),
    .AGBo(u_comparador_85_agbo), .AEBo(u_comparador_85_aebo));
  LED led_1 (.in(u_comparador_85_albo));
  LED led_2 (.in(u_comparador_85_agbo));
  LED led_3 (.in(u_comparador_85_aebo));
endmodule
