// Digital circuit contador_163_testado.dig as structural Verilog
module contador_163_testado (
  input  in_2,
  input  in_3,
  input  in_4,
  input  in_5,
  input  [3:0] in_6,
  output [3:0] out_1
);

  wire button_1_out, u_contador_163_rco;

  Button button_1 (.out(button_1_out));
  contador_163 #(.applicationType("IVERILOG"), .CodeFile("C:\\Users\\gabri\\CODE\\VERILOG\\QUARTUS\\LAB02\\contador_163.v")) u_contador_163 (
    .clock(button_1_out), .clr(in_2), .ld(in_3), .ent(in_4), .enp(in_5), .D(in_6), .Q(out_1),
    .rco(u_contador_163_rco));
  LED led_1 (.in(u_contador_163_rco));
endmodule
